// Digital circuit debug_level2.dig as structural Verilog
module debug_level2 (
  output [1:0] rs,
  output [1:0] rd,
  output [15:0] a,
  output [15:0] b,
  output [15:0] a_2
);

  wire add;

  LED jump (.in(add));
  LED u_add (.in(add));

  assign a_2 = a;

  // Notes on the sheet:
  //   r
  //   pc=
  //   =
  //   +
  //   ( r
  //   )
endmodule
