// Digital circuit decoder.dig as structural Verilog
module decoder (
  input  d_prog,
  input  [31:0] bypass,
  input  [31:0] d_inst,
  output [15:0] d_a,
  output [1:0] d_rs,
  output [1:0] d_rd,
  output d_jump,
  output d_add
);

  wire [31:18] multiplexer_1_out;

  Multiplexer #(.Bits(32)) multiplexer_1 (
    .sel(d_prog), .in_0(d_inst), .in_1(bypass),
    .out({multiplexer_1_out[31:22], d_rs, multiplexer_1_out[19:18], d_rd, d_a}));
  Decoder #(.Selector_Bits(3)) decoder_1 (
    .sel(multiplexer_1_out[26:24]), .out_0(d_add), .out_7(d_jump));  // open: out_1, out_2, out_3, out_4, out_5, out_6

  // Notes on the sheet:
  //   d_prog: decoder's input recieved from DIP.
  //   d_a: value or a reached in the decoder block.
endmodule
