// Digital circuit execute.dig as structural Verilog
module execute (
  input  [15:0] exe_a,
  input  [15:0] exe_b,
  input  exe_add,
  output [15:0] exe_result
);

  wire [15:0] add_1_s;

  Add #(.Bits(16)) add_1 (.a(exe_a), .b(exe_b), .c_i(1'b0), .s(add_1_s));  // open: c_o
  Multiplexer #(.Bits(16)) multiplexer_1 (.sel(exe_add), .in_0(exe_b), .in_1(add_1_s), .out(exe_result));
endmodule
