// Digital circuit level1.dig as structural Verilog
module level1 (
  input  [15:0] a,
  input  [7:0] sd,
  input  [15:0] a_2,
  input  [15:0] a_3,
  input  [15:0] a_4,
  input  [7:0] sd_2,
  input  [7:0] sd_3,
  input  [7:0] sd_4,
  output [15:0] b,
  output [15:0] r0,
  output [15:0] r1,
  output [15:0] r2,
  output [15:0] r3
);

  wire button_1_out, decoder_1_p2;
  wire [1:0] decoder_1_p3, decoder_1_p4, pc_out;
  wire [15:0] execute_1_p3;
  wire [31:0] multiplexer_1_out;

  Multiplexer #(.Selector_Bits(2), .Bits(32)) multiplexer_1 (
    .sel(pc_out), .in_0({{8{1'b0}}, sd, a}), .in_1({{8{1'b0}}, sd_3, a_2}), .in_2({{8{1'b0}}, sd_4, a_3}),
    .in_3({{8{1'b0}}, sd_2, a_4}), .out(multiplexer_1_out));
  // decoder decoder_1: pin names not known; wires that end beside it: multiplexer_1_out, decoder_1_p2, decoder_1_p3, decoder_1_p4
  Counter #(.Bits(2)) pc (.en(1'b1), .C(button_1_out), .clr(1'b0), .out(pc_out));  // open: ovf
  Button button_1 (.out(button_1_out));
  // execute execute_1: pin names not known; wires that end beside it: decoder_1_p2, b, execute_1_p3
  regfile regfile_1 (
    .rs(decoder_1_p3), .rd(decoder_1_p4), .result(execute_1_p3), .clk(button_1_out), .b(b), .r0(r0), .r1(r1),
    .r2(r2), .r3(r3));

  // Notes on the sheet:
  //   a: default 10
  //   sd: default 1
  //   a_2: default 21
  //   a_3: default 98
  //   a_4: default 92
  //   sd_2: default 48
  //   sd_3: default 18
  //   sd_4: default 35
endmodule
