// Digital circuit level2.dig as structural Verilog
module level2 (
  input  [15:0] value,
  input  [1:0] src,
  input  [1:0] dest,
  output [15:0] o_b,
  output [15:0] o_r0,
  output [15:0] o_r1,
  output [15:0] o_r2,
  output [15:0] o_r3,
  output [1:0] rs,
  output [1:0] rd,
  output [15:0] a,
  output [15:0] b,
  output [3:0] pc,
  output [15:0] a_2
);

  wire add, add_out, advance_out, assembler_1_store_clk, jump, jump_out, prog_out;
  wire [15:0] execute_1_exe_result;
  wire [31:0] assembler_1_inst, program_d;

  LED programming (.in(prog_out));
  DipSwitch prog (.out(prog_out));
  Button u_add (.out(add_out));
  Button u_jump (.out(jump_out));
  Button advance (.out(advance_out));
  assembler assembler_1 (
    .mode(prog_out), .value(value), .dest(dest), .src(src), .asm_add(add_out), .asm_jump(jump_out),
    .inst(assembler_1_inst), .store_clk(assembler_1_store_clk));
  // ScopeTrigger scopetrigger_1: pin names not known; wires that end beside it: advance_out
  LED jump_2 (.in(add));
  LED add_2 (.in(add));
  EEPROMDualPort #(.AddrBits(4), .Bits(32)) \program  (
    .A(pc), .Din(assembler_1_inst), .str(1'b1), .C(assembler_1_store_clk), .ld(1'b1), .D(program_d));
  CounterPreset #(.Bits(4), .isProgramCounter("true")) u_pc (
    .en(1'b1), .C(advance_out), .dir(1'b0), .in(a[3:0]), .ld(jump), .clr(1'b0), .out(pc));  // open: ovf
  decoder decoder_1 (
    .d_prog(prog_out), .bypass(assembler_1_inst), .d_inst(program_d), .d_a(a), .d_rs(rs), .d_rd(rd),
    .d_jump(jump), .d_add(add));
  execute execute_1 (.exe_a(a), .exe_b(b), .exe_add(add), .exe_result(execute_1_exe_result));
  regfile regfile_1 (
    .rs(rs), .rd(rd), .result(execute_1_exe_result), .clk(advance_out), .b(b), .r0(o_r0), .r1(o_r1),
    .r2(o_r2), .r3(o_r3));

  assign a_2 = a;
  assign o_b = b;

  // Notes on the sheet:
  //   r
  //   pc=
  //   =
  //   contents of program (hex, n*v repeats v):
  //   0,7000000,10001,7010001
  //   +
  //   ( r
  //   )
endmodule
