// Digital circuit regfile.dig as structural Verilog
module regfile (
  input  [1:0] rs,
  input  [1:0] rd,
  input  [15:0] result,
  input  clk,
  output [15:0] b,
  output [15:0] r0,
  output [15:0] r1,
  output [15:0] r2,
  output [15:0] r3
);

  wire decoder_1_out_0, decoder_1_out_1, decoder_1_out_2, decoder_1_out_3;
  wire [15:0] demultiplexer_1_out_0, demultiplexer_1_out_1, demultiplexer_1_out_2, demultiplexer_1_out_3;

  Demultiplexer #(.Selector_Bits(2), .Bits(16)) demultiplexer_1 (
    .sel(rd), .in(result), .out_0(demultiplexer_1_out_0), .out_1(demultiplexer_1_out_1),
    .out_2(demultiplexer_1_out_2), .out_3(demultiplexer_1_out_3));
  Decoder #(.Selector_Bits(2)) decoder_1 (
    .sel(rd), .out_0(decoder_1_out_0), .out_1(decoder_1_out_1), .out_2(decoder_1_out_2),
    .out_3(decoder_1_out_3));
  Register #(.Bits(16)) u_r0 (.D(demultiplexer_1_out_0), .C(clk), .en(decoder_1_out_0), .Q(r0));
  Register #(.Bits(16)) u_r1 (.D(demultiplexer_1_out_1), .C(clk), .en(decoder_1_out_1), .Q(r1));
  Register #(.Bits(16)) u_r2 (.D(demultiplexer_1_out_2), .C(clk), .en(decoder_1_out_2), .Q(r2));
  Register #(.Bits(16)) u_r3 (.D(demultiplexer_1_out_3), .C(clk), .en(decoder_1_out_3), .Q(r3));
  Multiplexer #(.Selector_Bits(2), .Bits(16)) multiplexer_1 (
    .sel(rs), .in_0(r0), .in_1(r1), .in_2(r2), .in_3(r3), .out(b));
endmodule
